// Logisim project Lap1_TN1.circ as structural Verilog: 1 circuit, main circuit main
module main (
  input  A,
  input  B,
  input  C,
  output NOT,
  output AND,
  output OR,
  output NAND,
  output NAND_2,
  output NOR,
  output XOR,
  output XNOR,
  output XOR_2,
  output NAND_3
);

  not not_1 (NOT, A);
  and and_1 (AND, A, B);
  or or_1 (OR, A, B);
  nand nand_1 (NAND, A, B);
  nor nor_1 (NOR, A, B);
  xor xor_1 (XOR, A, B);
  xnor xnor_1 (XNOR, A, B);
  xor u_xor_2 (XOR_2, A, B, C);
  nand u_nand_2 (NAND_3, B, A, C);
  nand u_nand_3 (NAND_2, NAND, C);
endmodule
